# Fritzing sketch cpen291p2 (saved by Fritzing 0.9.3b)
breadboards: 1

parts:
  Raspberry_Pi_1 = Raspberry Pi 3 [part_number=RPI-3-V1.2]  # not connected
  Part1 = Adafruit DC+Stepper Motor HAT [part_number="Adafruit #2348"]
  J1 = Basic Servo
  J2 = Basic Servo
  M1 = DC Motor
  M2 = DC Motor
  CAMERA1 = TTL Serial JPEG Camera  # not connected
  U6 = Voltage Regulator - 5V [package="TO220 [THT]"]
  C1 = Ceramic Capacitor [capacitance=0.1nF package="100 mil [THT, multilayer]"]
  C2 = Ceramic Capacitor [capacitance=0.1nF package="100 mil [THT, multilayer]"]
  VCC1 = 4 x AAA Battery Mount
  U13 = TCRT5000 [package=THT]
  U16 = TCRT5000 [package=THT]
  R22 = Resistor [tolerance=±5% resistance=10k package="2512 [SMD]"]
  R24 = Resistor [tolerance=±5% resistance=10k package="2512 [SMD]"]
  R18 = Resistor [tolerance=±5% resistance=150 package="2512 [SMD]"]
  R25 = Resistor [tolerance=±5% resistance=150 package="2512 [SMD]"]

nets:
  N1: Part1.M2A, M2.pin_2
  N2: Part1.M2B, M2.pin_1
  N3: Part1.M1B, M1.pin_1
  N4: Part1.M1A, M1.pin_2
  GND: Part1.GND, J1.gnd, J2.gnd, U6.GND, C1.1, C2.0, VCC1.-, U13.Pin_2, U13.Pin_3, U16.Pin_2, U16.Pin_3
  N5: Part1.VMOTOR, U6.input_voltage, C1.0, VCC1.+
  N6: Part1.5.0V, R22.Pin_0, R24.Pin_0, R18.Pin_0, R25.Pin_0
  N7: Part1.GPIO6, U16.Pin_1, R22.Pin_1
  N8: Part1.GPIO13, U13.Pin_1, R24.Pin_1
  N9: Part1.GPIO19, J2.pulse
  N10: Part1.GPIO26, J1.pulse
  VCC: J1.vcc, J2.vcc, U6.output_voltage, C2.1
  N11: U13.Pin_4, R18.Pin_1
  N12: U16.Pin_4, R25.Pin_1

custom parts:
  Adafruit DC+Stepper Motor HAT: Let your robotic dreams come true with the new DC+Stepper Motor HAT from Adafruit. This Raspberry Pi add-on is perfect for any motion project as it can drive up to 4 DC or 2 Stepper motors with full PWM speed control. Since the Raspberry Pi does not have a lot of PWM pins, we use a fully-dedicated PWM driver chip onboard to both control motor direction and speed. This chip handles all the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
  TTL Serial JPEG Camera: TTL Serial JPEG Camera with NTSC Out
  TCRT5000: TCRT5000 optical reflective sensor
